# Fritzing sketch Schematic (saved by Fritzing 0.9.3b)
breadboards: 1

parts:
  Part1 = Arduino Uno (Rev3)
  Part2 = Ambient Light Sensor (TEMT6000 Breakout Board)
  OLED_I2C1 = OLED 128x64 I2C Monochrome Display

nets:
  N1: Part1.A0, Part2.S
  N2: Part1.A4/SDA, OLED_I2C1.SDA
  N3: Part1.A5/SCL, OLED_I2C1.SCK
  3V3: Part1.AREF, Part1.3V3, Part2.VCC, OLED_I2C1.VDD
  GND: Part1.GND, Part2.GND, OLED_I2C1.GND
